// Logisim project Main.circ as structural Verilog: 24 circuits, main circuit main
module main (
  input  clkin,
  output clk,
  output clks,
  output clke
);

  wire j_k_ff_1_qn, nand_1_out;

  J_K_Flip_Flop j_k_ff_1 (.J(1'b1), .clk(clkin), .K(1'b1), .Q(clk), .Qn(j_k_ff_1_qn));  // open: preset, en, reset
  nand nand_1 (nand_1_out, clkin, clk);
  nand nand_2 (clke, j_k_ff_1_qn, clkin);
  not not_1 (clks, nand_1_out);
endmodule

module _1_Bit_Memory_Cell (
  input  s,
  input  e,
  output q
);

  wire nand_1_out, nand_2_out, nand_4_out;

  nand nand_1 (nand_1_out, s, e);
  nand nand_2 (nand_2_out, nand_1_out, e);
  nand nand_3 (q, nand_1_out, nand_4_out);
  nand nand_4 (nand_4_out, q, nand_2_out);
endmodule

module _8_Bit_Memory_Cell (
  input  [7:0] in_1,
  input  in_2,
  output [7:0] out_3
);

  _1_Bit_Memory_Cell u_1_bit_memory_cell_1 (.s(in_1[0]), .e(in_2), .q(out_3[0]));
  _1_Bit_Memory_Cell u_1_bit_memory_cell_2 (.s(in_1[1]), .e(in_2), .q(out_3[1]));
  _1_Bit_Memory_Cell u_1_bit_memory_cell_3 (.s(in_1[2]), .e(in_2), .q(out_3[2]));
  _1_Bit_Memory_Cell u_1_bit_memory_cell_4 (.s(in_1[3]), .e(in_2), .q(out_3[3]));
  _1_Bit_Memory_Cell u_1_bit_memory_cell_5 (.s(in_1[4]), .e(in_2), .q(out_3[4]));
  _1_Bit_Memory_Cell u_1_bit_memory_cell_6 (.s(in_1[5]), .e(in_2), .q(out_3[5]));
  _1_Bit_Memory_Cell u_1_bit_memory_cell_7 (.s(in_1[6]), .e(in_2), .q(out_3[6]));
  _1_Bit_Memory_Cell u_1_bit_memory_cell_8 (.s(in_1[7]), .e(in_2), .q(out_3[7]));
endmodule

module CPU_Enable (
  input  [7:0] in_1,
  input  in_2,
  output [7:0] out_3
);

  and and_1 (out_3[0], in_2, in_1[0]);
  and and_2 (out_3[1], in_2, in_1[1]);
  and and_3 (out_3[2], in_2, in_1[2]);
  and and_4 (out_3[3], in_2, in_1[3]);
  and and_5 (out_3[4], in_2, in_1[4]);
  and and_6 (out_3[5], in_2, in_1[5]);
  and and_7 (out_3[6], in_2, in_1[6]);
  and and_8 (out_3[7], in_2, in_1[7]);
endmodule

module CPU_Register_8_bit (
  input  [7:0] in_1,
  input  s,
  input  e,
  output [7:0] out_4,
  output [7:0] out_5
);

  wire [7:0] cpu_enable_1_out_3;

  _8_Bit_Memory_Cell u_8_bit_memory_cell_1 (.in_1(in_1), .out_3(out_4), .in_2(s));
  CPU_Enable cpu_enable_1 (.in_1(out_4), .out_3(cpu_enable_1_out_3), .in_2(e));
  assign out_5 = e ? cpu_enable_1_out_3 : 8'bz;  // Controlled_Buffer controlled_buffer_1
endmodule

module _4x16_Decoder (
  input  [3:0] in_1,
  output out_2,
  output out_3,
  output out_4,
  output out_5,
  output out_6,
  output out_7,
  output out_8,
  output out_9,
  output out_10,
  output out_11,
  output out_12,
  output out_13,
  output out_14,
  output out_15,
  output out_16,
  output out_17
);

  wire not_1_out, not_2_out, not_3_out, not_4_out;

  not not_1 (not_1_out, in_1[3]);
  not not_2 (not_2_out, in_1[2]);
  not not_3 (not_3_out, in_1[1]);
  not not_4 (not_4_out, in_1[0]);
  and _0000 (out_2, not_1_out, not_2_out, not_3_out, not_4_out);
  and _0001 (out_3, not_1_out, not_2_out, not_3_out, in_1[0]);
  and _0010 (out_4, not_1_out, not_2_out, in_1[1], not_4_out);
  and _0011 (out_5, not_1_out, not_2_out, in_1[1], in_1[0]);
  and _0100 (out_6, not_1_out, in_1[2], not_3_out, not_4_out);
  and _0101 (out_7, not_1_out, in_1[2], not_3_out, in_1[0]);
  and _0110 (out_8, not_1_out, in_1[2], in_1[1], not_4_out);
  and _0111 (out_9, not_1_out, in_1[2], in_1[1], in_1[0]);
  and _1000 (out_10, in_1[3], not_2_out, not_3_out, not_4_out);
  and _1001 (out_11, in_1[3], not_2_out, not_3_out, in_1[0]);
  and _1010 (out_12, in_1[3], not_2_out, in_1[1], not_4_out);
  and _1011 (out_13, in_1[3], not_2_out, in_1[1], in_1[0]);
  and _1100 (out_14, in_1[3], in_1[2], not_3_out, not_4_out);
  and _1101 (out_15, in_1[3], in_1[2], not_3_out, in_1[0]);
  and _1110 (out_16, in_1[3], in_1[2], in_1[1], not_4_out);
  and _1111 (out_17, in_1[3], in_1[2], in_1[1], in_1[0]);
endmodule

module RAM_1_Byte_Cell (
  input  [7:0] Input,
  input  RESET,
  input  H,
  input  V,
  input  S,
  input  E,
  output [7:0] Output,
  output [7:0] Stored_Value
);

  wire and_1_out, and_2_out, and_3_out, or_1_out;
  wire [7:0] cpu_register_8_bit_1_out_5;

  and and_1 (and_1_out, H, V);
  and and_2 (and_2_out, and_1_out, S);
  and and_3 (and_3_out, and_1_out, E);
  or or_1 (or_1_out, RESET, and_2_out);
  CPU_Register_8_bit cpu_register_8_bit_1 (
    .in_1(Input), .out_5(cpu_register_8_bit_1_out_5), .s(or_1_out), .e(and_3_out), .out_4(Stored_Value));
  assign Output = E ? cpu_register_8_bit_1_out_5 : 8'bz;  // Controlled_Buffer controlled_buffer_1
endmodule

module _2x4_Decoder (
  input  [1:0] in_1,
  output out_2,
  output out_3,
  output out_4,
  output out_5
);

  wire not_1_out, not_2_out;

  not not_1 (not_1_out, in_1[1]);
  not not_2 (not_2_out, in_1[0]);
  and _00 (out_2, not_1_out, not_2_out);
  and _01 (out_3, not_1_out, in_1[0]);
  and _10 (out_4, in_1[1], not_2_out);
  and _11 (out_5, in_1[1], in_1[0]);
endmodule

module RAM_256_Bytes (
  input  Reset,
  input  SA,
  input  [7:0] Address,
  input  [7:0] Input,
  input  S,
  input  E,
  output [7:0] out_7,
  output [7:0] out_8,
  output [7:0] out_9,
  output [7:0] out_10,
  output [7:0] out_11,
  output [7:0] out_12,
  output [7:0] out_13,
  output [7:0] out_14,
  output [7:0] Output,
  output [7:0] out_16,
  output [7:0] out_17,
  output [7:0] out_18,
  output [7:0] out_19,
  output [7:0] out_20,
  output [7:0] out_21,
  output [7:0] out_22,
  output [7:0] out_23
);

  wire n4x16_decoder_1_out_2, n4x16_decoder_1_out_3, n4x16_decoder_1_out_4, n4x16_decoder_1_out_5,
       n4x16_decoder_2_out_2, n4x16_decoder_2_out_3, n4x16_decoder_2_out_4, n4x16_decoder_2_out_5;
  wire [7:0] n8_bit_memory_cell_1_out_3, ram_1_byte_cell_1_output;

  _8_Bit_Memory_Cell u_8_bit_memory_cell_1 (.in_1(Address), .out_3(n8_bit_memory_cell_1_out_3), .in_2(SA));
  assign Output = E ? ram_1_byte_cell_1_output : 8'bz;  // Controlled_Buffer controlled_buffer_1
  _4x16_Decoder u_4x16_decoder_1 (
    .in_1(n8_bit_memory_cell_1_out_3[7:4]), .out_2(n4x16_decoder_1_out_2), .out_3(n4x16_decoder_1_out_3),
    .out_4(n4x16_decoder_1_out_4), .out_5(n4x16_decoder_1_out_5));  // open: out_6, out_7, out_8, out_9, out_10, out_11, out_12, out_13, out_14, out_15, out_16, out_17
  RAM_1_Byte_Cell ram_1_byte_cell_1 (
    .H(n4x16_decoder_1_out_2), .V(n4x16_decoder_2_out_5), .RESET(Reset), .Input(Input),
    .Output(ram_1_byte_cell_1_output), .S(S), .E(E), .Stored_Value(out_7));
  RAM_1_Byte_Cell ram_1_byte_cell_2 (
    .H(n4x16_decoder_1_out_3), .V(n4x16_decoder_2_out_5), .RESET(Reset), .Input(Input),
    .Output(ram_1_byte_cell_1_output), .S(S), .E(E), .Stored_Value(out_11));
  RAM_1_Byte_Cell ram_1_byte_cell_3 (
    .H(n4x16_decoder_1_out_4), .V(n4x16_decoder_2_out_5), .RESET(Reset), .Input(Input),
    .Output(ram_1_byte_cell_1_output), .S(S), .E(E), .Stored_Value(out_16));
  RAM_1_Byte_Cell ram_1_byte_cell_4 (
    .H(n4x16_decoder_1_out_5), .V(n4x16_decoder_2_out_5), .RESET(Reset), .Input(Input),
    .Output(ram_1_byte_cell_1_output), .S(S), .E(E), .Stored_Value(out_20));
  _4x16_Decoder u_4x16_decoder_2 (
    .in_1(n8_bit_memory_cell_1_out_3[3:0]), .out_2(n4x16_decoder_2_out_2), .out_3(n4x16_decoder_2_out_3),
    .out_4(n4x16_decoder_2_out_4), .out_5(n4x16_decoder_2_out_5));  // open: out_6, out_7, out_8, out_9, out_10, out_11, out_12, out_13, out_14, out_15, out_16, out_17
  RAM_1_Byte_Cell ram_1_byte_cell_5 (
    .H(n4x16_decoder_1_out_2), .V(n4x16_decoder_2_out_4), .RESET(Reset), .Input(Input),
    .Output(ram_1_byte_cell_1_output), .S(S), .E(E), .Stored_Value(out_8));
  RAM_1_Byte_Cell ram_1_byte_cell_6 (
    .H(n4x16_decoder_1_out_3), .V(n4x16_decoder_2_out_4), .RESET(Reset), .Input(Input),
    .Output(ram_1_byte_cell_1_output), .S(S), .E(E), .Stored_Value(out_12));
  RAM_1_Byte_Cell ram_1_byte_cell_7 (
    .H(n4x16_decoder_1_out_4), .V(n4x16_decoder_2_out_4), .RESET(Reset), .Input(Input),
    .Output(ram_1_byte_cell_1_output), .S(S), .E(E), .Stored_Value(out_17));
  RAM_1_Byte_Cell ram_1_byte_cell_8 (
    .H(n4x16_decoder_1_out_5), .V(n4x16_decoder_2_out_4), .RESET(Reset), .Input(Input),
    .Output(ram_1_byte_cell_1_output), .S(S), .E(E), .Stored_Value(out_21));
  RAM_1_Byte_Cell ram_1_byte_cell_9 (
    .H(n4x16_decoder_1_out_2), .V(n4x16_decoder_2_out_3), .RESET(Reset), .Input(Input),
    .Output(ram_1_byte_cell_1_output), .S(S), .E(E), .Stored_Value(out_9));
  RAM_1_Byte_Cell ram_1_byte_cell_10 (
    .H(n4x16_decoder_1_out_3), .V(n4x16_decoder_2_out_3), .RESET(Reset), .Input(Input),
    .Output(ram_1_byte_cell_1_output), .S(S), .E(E), .Stored_Value(out_13));
  RAM_1_Byte_Cell ram_1_byte_cell_11 (
    .H(n4x16_decoder_1_out_4), .V(n4x16_decoder_2_out_3), .RESET(Reset), .Input(Input),
    .Output(ram_1_byte_cell_1_output), .S(S), .E(E), .Stored_Value(out_18));
  RAM_1_Byte_Cell ram_1_byte_cell_12 (
    .H(n4x16_decoder_1_out_5), .V(n4x16_decoder_2_out_3), .RESET(Reset), .Input(Input),
    .Output(ram_1_byte_cell_1_output), .S(S), .E(E), .Stored_Value(out_22));
  RAM_1_Byte_Cell ram_1_byte_cell_13 (
    .H(n4x16_decoder_1_out_2), .V(n4x16_decoder_2_out_2), .RESET(Reset), .Input(Input),
    .Output(ram_1_byte_cell_1_output), .S(S), .E(E), .Stored_Value(out_10));
  RAM_1_Byte_Cell ram_1_byte_cell_14 (
    .H(n4x16_decoder_1_out_3), .V(n4x16_decoder_2_out_2), .RESET(Reset), .Input(Input),
    .Output(ram_1_byte_cell_1_output), .S(S), .E(E), .Stored_Value(out_14));
  RAM_1_Byte_Cell ram_1_byte_cell_15 (
    .H(n4x16_decoder_1_out_4), .V(n4x16_decoder_2_out_2), .RESET(Reset), .Input(Input),
    .Output(ram_1_byte_cell_1_output), .S(S), .E(E), .Stored_Value(out_19));
  RAM_1_Byte_Cell ram_1_byte_cell_16 (
    .H(n4x16_decoder_1_out_5), .V(n4x16_decoder_2_out_2), .RESET(Reset), .Input(Input),
    .Output(ram_1_byte_cell_1_output), .S(S), .E(E), .Stored_Value(out_23));
endmodule

module HalfAdder (
  input  in_1,
  input  in_2,
  output out_3,
  output out_4
);

  xor xor_1 (out_3, in_1, in_2);
  and and_1 (out_4, in_1, in_2);
endmodule

module FullAdder (
  input  a,
  input  b,
  input  carry_in,
  output sum,
  output carry_out
);

  wire halfadder_1_out_3, halfadder_1_out_4, halfadder_2_out_4;

  HalfAdder halfadder_1 (.in_1(a), .in_2(b), .out_3(halfadder_1_out_3), .out_4(halfadder_1_out_4));
  HalfAdder halfadder_2 (.in_1(halfadder_1_out_3), .in_2(carry_in), .out_3(sum), .out_4(halfadder_2_out_4));
  or or_1 (carry_out, halfadder_2_out_4, halfadder_1_out_4);
endmodule

module _8bit_Adder (
  input  [7:0] in_1,
  input  [7:0] in_2,
  input  Carry_in,
  output carry_out,
  output [7:0] out_5
);

  wire fulladder_2_carry_out, fulladder_3_carry_out, fulladder_4_carry_out, fulladder_5_carry_out,
       fulladder_6_carry_out, fulladder_7_carry_out, fulladder_8_carry_out;

  FullAdder fulladder_1 (
    .a(in_1[7]), .b(in_2[7]), .carry_in(fulladder_2_carry_out), .sum(out_5[7]), .carry_out(carry_out));
  FullAdder fulladder_2 (
    .a(in_1[6]), .b(in_2[6]), .carry_in(fulladder_3_carry_out), .sum(out_5[6]),
    .carry_out(fulladder_2_carry_out));
  FullAdder fulladder_3 (
    .a(in_1[5]), .b(in_2[5]), .carry_in(fulladder_4_carry_out), .sum(out_5[5]),
    .carry_out(fulladder_3_carry_out));
  FullAdder fulladder_4 (
    .a(in_1[4]), .b(in_2[4]), .carry_in(fulladder_5_carry_out), .sum(out_5[4]),
    .carry_out(fulladder_4_carry_out));
  FullAdder fulladder_5 (
    .a(in_1[3]), .b(in_2[3]), .carry_in(fulladder_6_carry_out), .sum(out_5[3]),
    .carry_out(fulladder_5_carry_out));
  FullAdder fulladder_6 (
    .a(in_1[2]), .b(in_2[2]), .carry_in(fulladder_7_carry_out), .sum(out_5[2]),
    .carry_out(fulladder_6_carry_out));
  FullAdder fulladder_7 (
    .a(in_1[1]), .b(in_2[1]), .carry_in(fulladder_8_carry_out), .sum(out_5[1]),
    .carry_out(fulladder_7_carry_out));
  FullAdder fulladder_8 (
    .a(in_1[0]), .b(in_2[0]), .carry_in(Carry_in), .sum(out_5[0]), .carry_out(fulladder_8_carry_out));
endmodule

module ALU_ShiftLeft (
  input  shift_in,
  input  [7:0] in_2,
  output [7:0] out_3,
  output shift_out
);

  wire [6:0] cpu_register_8_bit_1_out_5;

  CPU_Register_8_bit cpu_register_8_bit_1 (
    .in_1(in_2), .out_5({shift_out, cpu_register_8_bit_1_out_5}), .s(1'b1), .e(1'b1));  // open: out_4
  CPU_Register_8_bit cpu_register_8_bit_2 (
    .in_1({cpu_register_8_bit_1_out_5, shift_in}), .out_5(out_3), .s(1'b1), .e(1'b1));  // open: out_4
endmodule

module ALU_8bit_NOT (
  input  [7:0] in_1,
  output [7:0] out_2
);

  not not_1 (out_2[0], in_1[0]);
  not not_2 (out_2[1], in_1[1]);
  not not_3 (out_2[2], in_1[2]);
  not not_4 (out_2[3], in_1[3]);
  not not_5 (out_2[4], in_1[4]);
  not not_6 (out_2[5], in_1[5]);
  not not_7 (out_2[6], in_1[6]);
  not not_8 (out_2[7], in_1[7]);
endmodule

module ALU_8bit_AND (
  input  [7:0] in_1,
  input  [7:0] in_2,
  output [7:0] out_3
);

  and and_1 (out_3[0], in_1[0], in_2[0]);
  and and_2 (out_3[1], in_1[1], in_2[1]);
  and and_3 (out_3[2], in_1[2], in_2[2]);
  and and_4 (out_3[3], in_1[3], in_2[3]);
  and and_5 (out_3[4], in_1[4], in_2[4]);
  and and_6 (out_3[5], in_1[5], in_2[5]);
  and and_7 (out_3[6], in_1[6], in_2[6]);
  and and_8 (out_3[7], in_1[7], in_2[7]);
endmodule

module ALU_8bit_OR (
  input  [7:0] in_1,
  input  [7:0] in_2,
  output [7:0] out_3
);

  or or_1 (out_3[0], in_1[0], in_2[0]);
  or or_2 (out_3[1], in_1[1], in_2[1]);
  or or_3 (out_3[2], in_1[2], in_2[2]);
  or or_4 (out_3[3], in_1[3], in_2[3]);
  or or_5 (out_3[4], in_1[4], in_2[4]);
  or or_6 (out_3[5], in_1[5], in_2[5]);
  or or_7 (out_3[6], in_1[6], in_2[6]);
  or or_8 (out_3[7], in_1[7], in_2[7]);
endmodule

module ALU_1bit_LE (
  input  equal,
  input  a_larger,
  input  a,
  input  b,
  output carry_out,
  output equal_2,
  output a_larger_than_b
);

  wire and_2_out, not_1_out;

  xor xor_1 (carry_out, a, b);
  not not_1 (not_1_out, carry_out);
  and and_1 (equal_2, not_1_out, equal);
  and and_2 (and_2_out, equal, a, carry_out);
  or or_1 (a_larger_than_b, and_2_out, a_larger);
endmodule

module ALU_8bit_XOR (
  input  [7:0] in_1,
  input  [7:0] in_2,
  output equal,
  output a_larger,
  output [7:0] out_5
);

  wire alu_1bit_le_2_a_larger_than_b, alu_1bit_le_2_equal_2, alu_1bit_le_3_a_larger_than_b,
       alu_1bit_le_3_equal_2, alu_1bit_le_4_a_larger_than_b, alu_1bit_le_4_equal_2,
       alu_1bit_le_5_a_larger_than_b, alu_1bit_le_5_equal_2, alu_1bit_le_6_a_larger_than_b,
       alu_1bit_le_6_equal_2, alu_1bit_le_7_a_larger_than_b, alu_1bit_le_7_equal_2,
       alu_1bit_le_8_a_larger_than_b, alu_1bit_le_8_equal_2;

  ALU_1bit_LE alu_1bit_le_1 (
    .a(in_1[0]), .b(in_2[0]), .carry_out(out_5[0]), .equal(alu_1bit_le_2_equal_2),
    .a_larger(alu_1bit_le_2_a_larger_than_b), .equal_2(equal), .a_larger_than_b(a_larger));
  ALU_1bit_LE alu_1bit_le_2 (
    .a(in_1[1]), .b(in_2[1]), .carry_out(out_5[1]), .equal(alu_1bit_le_3_equal_2),
    .a_larger(alu_1bit_le_3_a_larger_than_b), .equal_2(alu_1bit_le_2_equal_2),
    .a_larger_than_b(alu_1bit_le_2_a_larger_than_b));
  ALU_1bit_LE alu_1bit_le_3 (
    .a(in_1[2]), .b(in_2[2]), .carry_out(out_5[2]), .equal(alu_1bit_le_4_equal_2),
    .a_larger(alu_1bit_le_4_a_larger_than_b), .equal_2(alu_1bit_le_3_equal_2),
    .a_larger_than_b(alu_1bit_le_3_a_larger_than_b));
  ALU_1bit_LE alu_1bit_le_4 (
    .a(in_1[3]), .b(in_2[3]), .carry_out(out_5[3]), .equal(alu_1bit_le_5_equal_2),
    .a_larger(alu_1bit_le_5_a_larger_than_b), .equal_2(alu_1bit_le_4_equal_2),
    .a_larger_than_b(alu_1bit_le_4_a_larger_than_b));
  ALU_1bit_LE alu_1bit_le_5 (
    .a(in_1[4]), .b(in_2[4]), .carry_out(out_5[4]), .equal(alu_1bit_le_6_equal_2),
    .a_larger(alu_1bit_le_6_a_larger_than_b), .equal_2(alu_1bit_le_5_equal_2),
    .a_larger_than_b(alu_1bit_le_5_a_larger_than_b));
  ALU_1bit_LE alu_1bit_le_6 (
    .a(in_1[5]), .b(in_2[5]), .carry_out(out_5[5]), .equal(alu_1bit_le_7_equal_2),
    .a_larger(alu_1bit_le_7_a_larger_than_b), .equal_2(alu_1bit_le_6_equal_2),
    .a_larger_than_b(alu_1bit_le_6_a_larger_than_b));
  ALU_1bit_LE alu_1bit_le_7 (
    .a(in_1[6]), .b(in_2[6]), .carry_out(out_5[6]), .equal(alu_1bit_le_8_equal_2),
    .a_larger(alu_1bit_le_8_a_larger_than_b), .equal_2(alu_1bit_le_7_equal_2),
    .a_larger_than_b(alu_1bit_le_7_a_larger_than_b));
  ALU_1bit_LE alu_1bit_le_8 (
    .a(in_1[7]), .b(in_2[7]), .carry_out(out_5[7]), .equal(1'b1), .a_larger(1'b0),
    .equal_2(alu_1bit_le_8_equal_2), .a_larger_than_b(alu_1bit_le_8_a_larger_than_b));
endmodule

module ALU_8bit_Zero (
  input  [7:0] in_1,
  output out_2
);

  wire or_1_out;

  or or_1 (or_1_out, in_1[0], in_1[1], in_1[2], in_1[3], in_1[4], in_1[5], in_1[6], in_1[7]);
  not not_1 (out_2, or_1_out);
endmodule

module ALU (
  input  [7:0] in_1,
  input  [7:0] in_2,
  input  carry_in,
  input  [2:0] instruction_code,
  output equal,
  output a_larger,
  output zero,
  output [7:0] out_8,
  output carry_out
);

  wire alu_shiftleft_1_shift_out, alu_shiftright_1_shift_out, and_1_out, and_2_out, and_3_out,
       n3x8_decoder_1_out_2, n3x8_decoder_1_out_3, n3x8_decoder_1_out_4, n3x8_decoder_1_out_5,
       n3x8_decoder_1_out_6, n3x8_decoder_1_out_7, n3x8_decoder_1_out_8, n8bit_adder_1_carry_out;
  wire [7:0] alu_8bit_and_1_out_3, alu_8bit_not_1_out_2, alu_8bit_or_1_out_3, alu_8bit_xor_1_out_5,
       alu_shiftleft_1_out_3, alu_shiftright_1_out_4, n8bit_adder_1_out_5;

  ALU_8bit_OR alu_8bit_or_1 (.in_1(in_1), .in_2(in_2), .out_3(alu_8bit_or_1_out_3));
  ALU_8bit_AND alu_8bit_and_1 (.in_1(in_1), .in_2(in_2), .out_3(alu_8bit_and_1_out_3));
  ALU_8bit_NOT alu_8bit_not_1 (.in_1(in_1), .out_2(alu_8bit_not_1_out_2));
  _8bit_Adder u_8bit_adder_1 (
    .carry_out(n8bit_adder_1_carry_out), .in_1(in_1), .in_2(in_2), .out_5(n8bit_adder_1_out_5),
    .Carry_in(carry_in));
  ALU_8bit_XOR alu_8bit_xor_1 (
    .in_1(in_1), .in_2(in_2), .out_5(alu_8bit_xor_1_out_5), .equal(equal), .a_larger(a_larger));
  ALU_ShiftLeft alu_shiftleft_1 (
    .in_2(in_1), .out_3(alu_shiftleft_1_out_3), .shift_out(alu_shiftleft_1_shift_out), .shift_in(carry_in));
  ALU_ShiftRight alu_shiftright_1 (
    .in_1(in_1), .shift_out(alu_shiftright_1_shift_out), .out_4(alu_shiftright_1_out_4), .shift_in(carry_in));
  _3x8_Decoder u_3x8_decoder_1 (
    .out_2(n3x8_decoder_1_out_2), .out_3(n3x8_decoder_1_out_3), .out_4(n3x8_decoder_1_out_4),
    .out_5(n3x8_decoder_1_out_5), .out_6(n3x8_decoder_1_out_6), .out_7(n3x8_decoder_1_out_7),
    .out_8(n3x8_decoder_1_out_8), .in_1(instruction_code));  // open: out_9
  Enabler enabler_1 (.in_1(alu_8bit_xor_1_out_5), .out_3(out_8), .in_2(n3x8_decoder_1_out_8));
  Enabler enabler_2 (.in_1(alu_8bit_or_1_out_3), .out_3(out_8), .in_2(n3x8_decoder_1_out_7));
  Enabler enabler_3 (.in_1(alu_8bit_and_1_out_3), .out_3(out_8), .in_2(n3x8_decoder_1_out_6));
  Enabler enabler_4 (.in_1(alu_8bit_not_1_out_2), .out_3(out_8), .in_2(n3x8_decoder_1_out_5));
  Enabler enabler_5 (.in_1(alu_shiftleft_1_out_3), .out_3(out_8), .in_2(n3x8_decoder_1_out_4));
  Enabler enabler_6 (.in_1(alu_shiftright_1_out_4), .out_3(out_8), .in_2(n3x8_decoder_1_out_3));
  Enabler enabler_7 (.in_1(n8bit_adder_1_out_5), .out_3(out_8), .in_2(n3x8_decoder_1_out_2));
  and and_1 (and_1_out, n3x8_decoder_1_out_4, alu_shiftleft_1_shift_out);
  and and_2 (and_2_out, n3x8_decoder_1_out_3, alu_shiftright_1_shift_out);
  and and_3 (and_3_out, n8bit_adder_1_carry_out, n3x8_decoder_1_out_2);
  assign carry_out = n3x8_decoder_1_out_4 ? and_1_out : 1'bz;  // Controlled_Buffer controlled_buffer_1
  assign carry_out = n3x8_decoder_1_out_3 ? and_2_out : 1'bz;  // Controlled_Buffer controlled_buffer_2
  assign carry_out = n3x8_decoder_1_out_2 ? and_3_out : 1'bz;  // Controlled_Buffer controlled_buffer_3
  ALU_8bit_Zero alu_8bit_zero_1 (.in_1(out_8), .out_2(zero));

  // Notes on the sheet:
  //   A
  //   B
endmodule

module ALU_ShiftRight (
  input  [7:0] in_1,
  input  shift_in,
  output shift_out,
  output [7:0] out_4
);

  wire [7:1] cpu_register_8_bit_1_out_5;

  CPU_Register_8_bit cpu_register_8_bit_1 (
    .in_1(in_1), .out_5({cpu_register_8_bit_1_out_5, shift_out}), .s(1'b1), .e(1'b1));  // open: out_4
  CPU_Register_8_bit cpu_register_8_bit_2 (
    .in_1({shift_in, cpu_register_8_bit_1_out_5}), .out_5(out_4), .s(1'b1), .e(1'b1));  // open: out_4
endmodule

module _3x8_Decoder (
  input  [2:0] in_1,
  output out_2,
  output out_3,
  output out_4,
  output out_5,
  output out_6,
  output out_7,
  output out_8,
  output out_9
);

  wire not_1_out, not_2_out, not_3_out;

  not not_1 (not_1_out, in_1[2]);
  not not_2 (not_2_out, in_1[1]);
  not not_3 (not_3_out, in_1[0]);
  and _000 (out_2, not_1_out, not_2_out, not_3_out);
  and _001 (out_3, not_1_out, not_2_out, in_1[0]);
  and _010 (out_4, not_1_out, in_1[1], not_3_out);
  and _011 (out_5, not_1_out, in_1[1], in_1[0]);
  and _100 (out_6, in_1[2], not_2_out, not_3_out);
  and _101 (out_7, in_1[2], not_2_out, in_1[0]);
  and _110 (out_8, in_1[2], in_1[1], not_3_out);
  and _111 (out_9, in_1[2], in_1[1], in_1[0]);
endmodule

module Enabler (
  input  [7:0] in_1,
  input  in_2,
  output [7:0] out_3
);

  wire and_1_out, and_2_out, and_3_out, and_4_out, and_5_out, and_6_out, and_7_out, and_8_out;

  and and_1 (and_1_out, in_2, in_1[0]);
  and and_2 (and_2_out, in_2, in_1[1]);
  and and_3 (and_3_out, in_2, in_1[2]);
  and and_4 (and_4_out, in_2, in_1[3]);
  and and_5 (and_5_out, in_2, in_1[4]);
  and and_6 (and_6_out, in_2, in_1[5]);
  and and_7 (and_7_out, in_2, in_1[6]);
  and and_8 (and_8_out, in_2, in_1[7]);
  assign out_3[0] = in_2 ? and_1_out : 1'bz;  // Controlled_Buffer controlled_buffer_1
  assign out_3[1] = in_2 ? and_2_out : 1'bz;  // Controlled_Buffer controlled_buffer_2
  assign out_3[2] = in_2 ? and_3_out : 1'bz;  // Controlled_Buffer controlled_buffer_3
  assign out_3[3] = in_2 ? and_4_out : 1'bz;  // Controlled_Buffer controlled_buffer_4
  assign out_3[4] = in_2 ? and_5_out : 1'bz;  // Controlled_Buffer controlled_buffer_5
  assign out_3[5] = in_2 ? and_6_out : 1'bz;  // Controlled_Buffer controlled_buffer_6
  assign out_3[6] = in_2 ? and_7_out : 1'bz;  // Controlled_Buffer controlled_buffer_7
  assign out_3[7] = in_2 ? and_8_out : 1'bz;  // Controlled_Buffer controlled_buffer_8
endmodule

module clock (
  input  clkin,
  output clk,
  output clks,
  output clke
);

  wire j_k_ff_1_qn, nand_1_out;

  J_K_Flip_Flop j_k_ff_1 (.J(1'b1), .clk(clkin), .K(1'b1), .Q(clk), .Qn(j_k_ff_1_qn));  // open: preset, en, reset
  nand nand_1 (nand_1_out, clkin, clk);
  nand nand_2 (clke, j_k_ff_1_qn, clkin);
  not not_1 (clks, nand_1_out);
endmodule
